# Fritzing sketch Basic Sketch (saved by Fritzing 0.9.3b)
breadboards: 1

parts:
  Part1 = Arduino Nano (Rev3.0) (ICSP)
  hc-sr1 = hc-sr04
  M1 = DC Motor
  M2 = DC Motor
  VCC1 = 4 x AAA Battery Mount
  IC1 = DIP - 8 pins [chip_label=IC package="DIP (Dual Inline) [THT]"]

nets:
  GND: Part1.GND, hc-sr1.GND, VCC1.-, IC1.GND
  N1: Part1.D5, IC1.B01
  N2: Part1.D6, IC1.A01
  N3: Part1.D9, IC1.A02
  N4: Part1.D10, IC1.B02
  N5: Part1.D12/MISO, hc-sr1.Echo
  VIN: Part1.VIN, VCC1.+, IC1.VCC
  5V: Part1.5V, hc-sr1.VCC
  N6: Part1.D13/SCK, hc-sr1.Trig
  N7: M1.pin_1, IC1.AIN1
  N8: M1.pin_2, IC1.AIN2
  N9: M2.pin_1, IC1.BIN1
  N10: M2.pin_2, IC1.BIN2

custom parts:
  DIP - 8 pins: A DIP stand-in part for whatever IC you want. With 8 pins on a 300mil dual inline package (DIP) footprint.
